// Logisim project uke9arkitektur.circ as structural Verilog
module counter (
);

  Register register_1 ();  // open: D, en, Q, clk, clr
endmodule

// FA
module Fulladder (
  input  A,
  input  B,
  input  C,
  output S_n,
  output C_1
);

  wire and_1_out, halfadder_1_c, halfadder_1_s;

  Halfadder halfadder_1 (.A(A), .B(B), .S(halfadder_1_s), .C(halfadder_1_c));
  xor xor_1 (S_n, halfadder_1_s, C);
  and and_1 (and_1_out, halfadder_1_s, C);
  or or_1 (C_1, and_1_out, halfadder_1_c);
endmodule

// HA
module Halfadder (
  input  A,
  input  B,
  output S,
  output C
);

  xor xor_1 (S, A, B);
  and and_1 (C, A, B);
endmodule
