// Logisim project MiniCPU.circ as structural Verilog: 4 circuits, main circuit main
module main (
);

  Instruksjons_Peker instruksjons_peker_1 ();  // open: Clk, RESET, out_3
  RAM ram_1 ();  // open: Adresse, Chip_select__0_disable_comp, Clk, RESET__on_1, Load_0___Write_1, Output, Input
  Register R ();  // open: D, en, Q, clk, clr
endmodule

// RAM (4)
module RAM (
  input  [3:0] Adresse,
  input  Chip_select__0_disable_comp,
  input  [3:0] Input,
  input  Clk,
  input  RESET__on_1,
  input  Load_0___Write_1,
  output [3:0] Output
);

  wire not_1_out;

  RAM_part #(.addrWidth(4), .dataWidth(4)) ram_1 (
    .addr(Adresse), .data(Output), .sel(Chip_select__0_disable_comp), .clk(Clk), .ld(not_1_out),
    .clr(RESET__on_1));
  assign Output = Load_0___Write_1 ? Input : 4'bz;  // Controlled_Buffer controlled_buffer_1
  not not_1 (not_1_out, Load_0___Write_1);
endmodule

// IP
module Instruksjons_Peker (
  input  Clk,
  input  RESET,
  output [3:0] out_3
);

  wire and_1_out, nand_1_out;

  nand nand_1 (nand_1_out, out_3[0], out_3[1], out_3[2], out_3[3]);
  and and_1 (and_1_out, nand_1_out, Clk);
  Counter counter_1 (.Clk(and_1_out), .Reset(RESET), .out_3(out_3));
endmodule

module Counter (
  input  Clk,
  input  Reset,
  output [3:0] out_3
);

  wire [3:0] register_1_q;

  Register #(.width(4)) register_1 (.D(out_3), .Q(register_1_q), .clk(Clk), .clr(Reset));  // open: en
  Adder #(.width(4)) adder_1 (.a(4'b0001), .b(register_1_q), .out(out_3));  // open: cin, cout
endmodule
